# Fritzing sketch thermometer (saved by Fritzing 0.9.3b)
breadboards: 1
stripboards: 1

parts:
  Gizwits_WiFi_Witty_ESP-12F1 = Gizwits WiFi Witty ESP-12F
  C4 = Ceramic Capacitor [capacitance=100nF package="100 mil [THT, multilayer]"]
  C5 = Electrolytic Capacitor [capacitance=0.47mF voltage=16V package="300 mil [THT, electrolytic]"]
  U3 = V_REG_LD1117VXX [package=78xxl]
  U4 = USB Connectors [package=usb-microb]
  Q3 = NPN-Transistor [package="SOT-23 [SMD]"]
  Q4 = NPN-Transistor [package="SOT-23 [SMD]"]
  R4 = Resistor [tolerance=±5% resistance=10k package=THT]
  R5 = Resistor [tolerance=±5% resistance=10k package=THT]
  IC2 = FT232RQ [package=qfn-32]
  C6 = Electrolytic Capacitor [capacitance=0.47mF voltage=16V package="300 mil [THT, electrolytic]"]
  R6 = Resistor [tolerance=±5% resistance=10k package=THT]
  R8 = Resistor [tolerance=±5% resistance=10k package=THT]
  DHT1 = DHT22 Humidity and Temperature Sensor
  Gizwits_WiFi_Witty_ESP-12F2 = Gizwits WiFi Witty ESP-12F
  S1 = Pushbutton [package="[THT]"]
  C9 = Ceramic Capacitor [capacitance=100nF package="100 mil [THT, multilayer]"]
  R11 = Resistor [tolerance=±5% resistance=10k package=THT]
  R12 = Resistor [tolerance=±5% resistance=10k package=THT]
  DHT2 = DHT22 Humidity and Temperature Sensor
  S2 = Pushbutton [package="[THT]"]
  U5 = V_REG_LD1117VXX [package=78xxl]
  U6 = USB Connectors [package=usb-microb]
  IC3 = FT232RQ [package=qfn-32]
  Q5 = NPN-Transistor [package="SOT-23 [SMD]"]
  Q6 = NPN-Transistor [package="SOT-23 [SMD]"]
  C8 = Electrolytic Capacitor [capacitance=0.47mF voltage=16V package="200 mil [THT, electrolytic]"]
  C7 = Electrolytic Capacitor [capacitance=0.47mF voltage=16V package="200 mil [THT, electrolytic]"]
  J3 = female pin header, 2 pins [form="♀ (female)"]
  J4 = male pin header, 6 pins [form="♂ (male)"]
  J2 = screw terminal, 3 pins
  R13 = Resistor [tolerance=±5% resistance=10k package=THT]
  R14 = Resistor [tolerance=±5% resistance=10k package=THT]

nets:
  N1: Gizwits_WiFi_Witty_ESP-12F1.REST, Q4.1, R8.Pin_0, S1.Pin_3, S1.Pin_4
  VCC: Gizwits_WiFi_Witty_ESP-12F1.VCC, C4.0, C5.+, U3.OUT, R6.Pin_0, DHT1.VDD
  GND: Gizwits_WiFi_Witty_ESP-12F1.GND, C4.1, C5.-, U3.GND, U4.GND, IC2.GND, C6.-, R8.Pin_1, DHT1.GND, S1.Pin_1, S1.Pin_2
  N2: Gizwits_WiFi_Witty_ESP-12F1.GPIO0, Q3.1, R6.Pin_1
  N3: Gizwits_WiFi_Witty_ESP-12F1.GPIO5, DHT1.DATA
  N4: Gizwits_WiFi_Witty_ESP-12F1.RXD, IC2.TXD
  N5: Gizwits_WiFi_Witty_ESP-12F1.TXD, IC2.RXD
  N6: U3.IN, U4.VBUS, C6.+
  N7: Q3.2, R5.Pin_1, IC2.DTR
  N8: Q3.0, R4.Pin_1
  N9: Q4.2, R4.Pin_0, IC2.RTS
  N10: Q4.0, R5.Pin_0
  N11: Gizwits_WiFi_Witty_ESP-12F2.REST, R11.Pin_1, S2.Pin_3, S2.Pin_4, Q6.1
  VCC_2: Gizwits_WiFi_Witty_ESP-12F2.VCC, C9.0, R11.Pin_0, DHT2.VDD, U5.OUT, C8.+, J2.pin1, R14.Pin_1
  GND_2: Gizwits_WiFi_Witty_ESP-12F2.GND, C9.1, DHT2.GND, S2.Pin_1, S2.Pin_2, U5.GND, U6.GND, IC3.GND, C8.-, C7.-, J3.pin2, J4.pin2, J2.pin3
  N12: Gizwits_WiFi_Witty_ESP-12F2.GPIO0, Q5.1, R14.Pin_0
  N13: Gizwits_WiFi_Witty_ESP-12F2.GPIO5, DHT2.DATA, J2.pin2
  N14: Gizwits_WiFi_Witty_ESP-12F2.RXD, IC3.TXD, J4.pin3
  N15: Gizwits_WiFi_Witty_ESP-12F2.TXD, IC3.RXD, J4.pin4
  N16: R12.Pin_0, IC3.DTR, Q5.2, J4.pin6
  N17: R12.Pin_1, Q6.0
  N18: U5.IN, U6.VBUS, C7.+, J3.pin1
  N19: IC3.RTS, Q6.2, J4.pin5, R13.Pin_1
  N20: Q5.0, R13.Pin_0
