# Fritzing sketch thermostat (saved by Fritzing 0.9.3b)
stripboards: 1
breadboards: 1

parts:
  Gizwits_WiFi_Witty_ESP-12F1 = Gizwits WiFi Witty ESP-12F
  KY-1 = Keyes Relay [package=THT]
  U1 = USB Connectors [package=usb-microb]
  U2 = V_REG_LD1117VXX [package=78xxl]
  C1 = Electrolytic Capacitor [capacitance=0.47mF voltage=16V package="300 mil [THT, electrolytic]"]
  C2 = Electrolytic Capacitor [capacitance=0.47mF voltage=16V package="300 mil [THT, electrolytic]"]
  C3 = Ceramic Capacitor [capacitance=100nF package="100 mil [THT, multilayer]"]
  Q1 = NPN-Transistor [package="TO92 [THT]"]
  Q2 = NPN-Transistor [package="TO92 [THT]"]
  R1 = Resistor [tolerance=±5% resistance=10k package=THT]
  R2 = Resistor [tolerance=±5% resistance=10k package=THT]
  IC1 = Single-Chip USB to UART Bridge [package=mlp28]
  Q4 = NPN-Transistor [package="TO92 [THT]"]
  R3 = Resistor [tolerance=±5% resistance=10k package=THT]
  R4 = Resistor [tolerance=±5% resistance=10k package=THT]
  DS1 = DS18B20 1-Wire Temperature Sensor [part_number=DS18B20]
  R5 = Resistor [tolerance=±5% resistance=4.7k package=THT]

nets:
  N1: Gizwits_WiFi_Witty_ESP-12F1.REST, Q2.C
  N2: Gizwits_WiFi_Witty_ESP-12F1.GPIO16, R3.Pin_0
  N3: Gizwits_WiFi_Witty_ESP-12F1.GPIO14, DS1.DQ, R5.Pin_0
  VCC: Gizwits_WiFi_Witty_ESP-12F1.VCC, U2.OUT, C1.+, C3.1, IC1.VBUS, DS1.VDD
  GND: Gizwits_WiFi_Witty_ESP-12F1.GND, KY-1.ground, U1.GND, U2.GND, C1.-, C2.-, C3.0, IC1.GND, Q4.E, R3.Pin_1, DS1.GND, R5.Pin_1
  N4: Gizwits_WiFi_Witty_ESP-12F1.GPIO0, Q1.C
  N5: Gizwits_WiFi_Witty_ESP-12F1.RXD, IC1.TXD
  N6: Gizwits_WiFi_Witty_ESP-12F1.TXD, IC1.RXD
  N7: KY-1.signal, Q4.C, R4.Pin_0
  N8: KY-1.power, U1.VBUS, U2.IN, C2.+, R4.Pin_1
  N9: Q1.E, R1.Pin_1, IC1.RTS
  N10: Q1.B, R2.Pin_1
  N11: Q2.E, R2.Pin_0, IC1.DTR
  N12: Q2.B, R1.Pin_0

custom parts:
  Keyes Relay: The Keyes 5V relay module is suitable for SCM development, home appliance control. It uses a 5V~12V TIL control signal which can control DC / AC signal.
