# Fritzing sketch thermostat_nodemcu (saved by Fritzing 0.9.3b)
stripboards: 1
breadboards: 1

parts:
  KY-1 = Keyes Relay [package=THT]
  Q4 = NPN-Transistor [package="TO92 [THT]"]
  R3 = Resistor [tolerance=±5% resistance=10k package=THT]
  R4 = Resistor [tolerance=±5% resistance=10k package=THT]
  DS1 = DS18B20 1-Wire Temperature Sensor [part_number=DS18B20]
  R5 = Resistor [tolerance=±5% resistance=4.7k package=THT]
  U3 = NodeMCU V3.0
  J3 = female pin header, 15 pins [form="♀ (female)"]
  J4 = female pin header, 15 pins [form="♀ (female)"]
  Q5 = NPN-Transistor [package="TO92 [THT]"]
  R6 = Resistor [tolerance=±5% resistance=10k package=THT]
  R7 = Resistor [tolerance=±5% resistance=10k package=THT]
  DS2 = DS18B20 1-Wire Temperature Sensor [part_number=DS18B20]
  R8 = Resistor [tolerance=±5% resistance=4.7k package=THT]
  KY-2 = Keyes Relay [package=THT]

nets:
  N1: KY-1.signal, Q4.C, R4.Pin_0
  N2: KY-1.power, R4.Pin_1, U3.VU
  N3: KY-1.ground, Q4.E, U3.GND#41
  N4: Q4.B, R3.Pin_0
  N5: R3.Pin_1, U3.D7
  N6: DS1.GND, R5.Pin_1, U3.GND#6, U3.GND#13, U3.GND#16, U3.GND#33
  N7: DS1.DQ, R5.Pin_0, U3.D6
  VDD: DS1.VDD, U3.3V3
  N8: J3.pin1, DS2.VDD, R8.Pin_0
  N9: J3.pin2, DS2.GND
  N10: J3.pin6, R7.Pin_1
  N11: J3.pin7, DS2.DQ, R8.Pin_1
  N12: J4.pin13, R6.Pin_1, KY-2.power
  N13: J4.pin14, Q5.E, KY-2.ground
  N14: Q5.B, R7.Pin_0
  N15: Q5.C, R6.Pin_0, KY-2.signal

custom parts:
  Keyes Relay: The Keyes 5V relay module is suitable for SCM development, home appliance control. It uses a 5V~12V TIL control signal which can control DC / AC signal.
  NodeMCU V3.0: ESP8266 based NodeMCU
